// Logisim project Main.circ as structural Verilog: 1 circuit, main circuit main
module main (
  input  [31:0] in_1,
  input  [31:0] in_2
);

  // Probe on in_2
  // Probe on in_1
  Adder #(.width(32)) adder_1 (.a(in_1), .b(in_2), .cin(1'b0));  // open: out, cout
  Subtractor #(.width(32)) subtractor_1 (.a(in_1), .b(in_2), .bin(1'b0));  // open: out, bout

  // Notes on the sheet:
  //   X_IN
  //   Y_IN
  //   无符号加法
  //    无符号减法
endmodule
