// Logisim project RF_32.circ as structural Verilog: 1 circuit, main circuit main
module main (
  input  [4:0] N1,
  input  [4:0] N2,
  input  [4:0] ND,
  input  [31:0] D_in,
  input  WRITEREG,
  input  CLK,
  input  RESET,
  output [31:0] Q1,
  output [31:0] Q2
);

  wire [7:0] decoder_1_out0, decoder_1_out8, decoder_1_out16, decoder_1_out24;
  wire [31:0] r0_q, r1_q, r2_q, r3_q, r4_q, r5_q, r6_q, r7_q, r8_q, r9_q, r10_q, r11_q, r12_q, r13_q, r14_q,
       r15_q, r16_q, r17_q, r18_q, r19_q, r20_q, r21_q, r22_q, r23_q, r24_q, r25_q, r26_q, r27_q, r28_q,
       r29_q, r30_q, r31_q;

  Decoder #(.select(5), .tristate("false"), .disabled(0), .enable("true")) decoder_1 (
    .out0(decoder_1_out0[0]), .out1(decoder_1_out0[1]), .out2(decoder_1_out0[2]), .out3(decoder_1_out0[3]),
    .out4(decoder_1_out0[4]), .out5(decoder_1_out0[5]), .out6(decoder_1_out0[6]), .out7(decoder_1_out0[7]),
    .out8(decoder_1_out8[0]), .out9(decoder_1_out8[1]), .out10(decoder_1_out8[2]), .out11(decoder_1_out8[3]),
    .out12(decoder_1_out8[4]), .out13(decoder_1_out8[5]), .out14(decoder_1_out8[6]),
    .out15(decoder_1_out8[7]), .out16(decoder_1_out16[0]), .out17(decoder_1_out16[1]),
    .out18(decoder_1_out16[2]), .out19(decoder_1_out16[3]), .out20(decoder_1_out16[4]),
    .out21(decoder_1_out16[5]), .out22(decoder_1_out16[6]), .out23(decoder_1_out16[7]),
    .out24(decoder_1_out24[0]), .out25(decoder_1_out24[1]), .out26(decoder_1_out24[2]),
    .out27(decoder_1_out24[3]), .out28(decoder_1_out24[4]), .out29(decoder_1_out24[5]),
    .out30(decoder_1_out24[6]), .out31(decoder_1_out24[7]), .sel(ND), .en(WRITEREG));
  Register #(.width(32), .trigger("rising"), .Select("low")) r0 (
    .D(D_in), .en(decoder_1_out0[0]), .Q(r0_q), .clk(CLK), .clr(1'b1));
  Register #(.width(32), .trigger("rising"), .Select("low")) r8 (
    .D(D_in), .en(decoder_1_out8[0]), .Q(r8_q), .clk(CLK), .clr(RESET));
  Register #(.width(32), .trigger("rising"), .Select("low")) r16 (
    .D(D_in), .en(decoder_1_out16[0]), .Q(r16_q), .clk(CLK), .clr(RESET));
  Register #(.width(32), .trigger("rising"), .Select("low")) r24 (
    .D(D_in), .en(decoder_1_out24[0]), .Q(r24_q), .clk(CLK), .clr(RESET));
  Register #(.width(32), .trigger("rising"), .Select("low")) r1 (
    .D(D_in), .en(decoder_1_out0[1]), .Q(r1_q), .clk(CLK), .clr(RESET));
  Register #(.width(32), .trigger("rising"), .Select("low")) r9 (
    .D(D_in), .en(decoder_1_out8[1]), .Q(r9_q), .clk(CLK), .clr(RESET));
  Register #(.width(32), .trigger("rising"), .Select("low")) r17 (
    .D(D_in), .en(decoder_1_out16[1]), .Q(r17_q), .clk(CLK), .clr(RESET));
  Register #(.width(32), .trigger("rising"), .Select("low")) r25 (
    .D(D_in), .en(decoder_1_out24[1]), .Q(r25_q), .clk(CLK), .clr(RESET));
  Register #(.width(32), .trigger("rising"), .Select("low")) r2 (
    .D(D_in), .en(decoder_1_out0[2]), .Q(r2_q), .clk(CLK), .clr(RESET));
  Register #(.width(32), .trigger("rising"), .Select("low")) r10 (
    .D(D_in), .en(decoder_1_out8[2]), .Q(r10_q), .clk(CLK), .clr(RESET));
  Register #(.width(32), .trigger("rising"), .Select("low")) r18 (
    .D(D_in), .en(decoder_1_out16[2]), .Q(r18_q), .clk(CLK), .clr(RESET));
  Register #(.width(32), .trigger("rising"), .Select("low")) r26 (
    .D(D_in), .en(decoder_1_out24[2]), .Q(r26_q), .clk(CLK), .clr(RESET));
  Register #(.width(32), .trigger("rising"), .Select("low")) r3 (
    .D(D_in), .en(decoder_1_out0[3]), .Q(r3_q), .clk(CLK), .clr(RESET));
  Register #(.width(32), .trigger("rising"), .Select("low")) r4 (
    .D(D_in), .en(decoder_1_out0[4]), .Q(r4_q), .clk(CLK), .clr(RESET));
  Register #(.width(32), .trigger("rising"), .Select("low")) r12 (
    .D(D_in), .en(decoder_1_out8[4]), .Q(r12_q), .clk(CLK), .clr(RESET));
  Register #(.width(32), .trigger("rising"), .Select("low")) r11 (
    .D(D_in), .en(decoder_1_out8[3]), .Q(r11_q), .clk(CLK), .clr(RESET));
  Register #(.width(32), .trigger("rising"), .Select("low")) r20 (
    .D(D_in), .en(decoder_1_out16[4]), .Q(r20_q), .clk(CLK), .clr(RESET));
  Register #(.width(32), .trigger("rising"), .Select("low")) r19 (
    .D(D_in), .en(decoder_1_out16[3]), .Q(r19_q), .clk(CLK), .clr(RESET));
  Register #(.width(32), .trigger("rising"), .Select("low")) r28 (
    .D(D_in), .en(decoder_1_out24[4]), .Q(r28_q), .clk(CLK), .clr(RESET));
  Register #(.width(32), .trigger("rising"), .Select("low")) r27 (
    .D(D_in), .en(decoder_1_out24[3]), .Q(r27_q), .clk(CLK), .clr(RESET));
  Register #(.width(32), .trigger("rising"), .Select("low")) r5 (
    .D(D_in), .en(decoder_1_out0[5]), .Q(r5_q), .clk(CLK), .clr(RESET));
  Register #(.width(32), .trigger("rising"), .Select("low")) r13 (
    .D(D_in), .en(decoder_1_out8[5]), .Q(r13_q), .clk(CLK), .clr(RESET));
  Register #(.width(32), .trigger("rising"), .Select("low")) r21 (
    .D(D_in), .en(decoder_1_out16[5]), .Q(r21_q), .clk(CLK), .clr(RESET));
  Register #(.width(32), .trigger("rising"), .Select("low")) r29 (
    .D(D_in), .en(decoder_1_out24[5]), .Q(r29_q), .clk(CLK), .clr(RESET));
  Register #(.width(32), .trigger("rising"), .Select("low")) r6 (
    .D(D_in), .en(decoder_1_out0[6]), .Q(r6_q), .clk(CLK), .clr(RESET));
  Register #(.width(32), .trigger("rising"), .Select("low")) r14 (
    .D(D_in), .en(decoder_1_out8[6]), .Q(r14_q), .clk(CLK), .clr(RESET));
  Register #(.width(32), .trigger("rising"), .Select("low")) r22 (
    .D(D_in), .en(decoder_1_out16[6]), .Q(r22_q), .clk(CLK), .clr(RESET));
  Register #(.width(32), .trigger("rising"), .Select("low")) r30 (
    .D(D_in), .en(decoder_1_out24[6]), .Q(r30_q), .clk(CLK), .clr(RESET));
  Register #(.width(32), .trigger("rising"), .Select("low")) r7 (
    .D(D_in), .en(decoder_1_out0[7]), .Q(r7_q), .clk(CLK), .clr(RESET));
  Register #(.width(32), .trigger("rising"), .Select("low")) r15 (
    .D(D_in), .en(decoder_1_out8[7]), .Q(r15_q), .clk(CLK), .clr(RESET));
  Register #(.width(32), .trigger("rising"), .Select("low")) r23 (
    .D(D_in), .en(decoder_1_out16[7]), .Q(r23_q), .clk(CLK), .clr(RESET));
  Register #(.width(32), .trigger("rising"), .Select("low")) r31 (
    .D(D_in), .en(decoder_1_out24[7]), .Q(r31_q), .clk(CLK), .clr(RESET));
  Multiplexer #(.select(5), .width(32), .disabled(0), .enable("false")) multiplexer_1 (
    .in0(r0_q), .in1(r1_q), .in2(r2_q), .in3(r3_q), .in4(r4_q), .in5(r5_q), .in6(r6_q), .in7(r7_q),
    .in8(r8_q), .in9(r9_q), .in10(r10_q), .in11(r11_q), .in12(r12_q), .in13(r13_q), .in14(r14_q),
    .in15(r15_q), .in16(r16_q), .in17(r17_q), .in18(r18_q), .in19(r19_q), .in20(r20_q), .in21(r21_q),
    .in22(r22_q), .in23(r23_q), .in24(r24_q), .in25(r25_q), .in26(r26_q), .in27(r27_q), .in28(r28_q),
    .in29(r29_q), .in30(r30_q), .in31(r31_q), .out(Q1), .sel(N1));
  Multiplexer #(.select(5), .width(32), .disabled(0), .enable("false")) multiplexer_2 (
    .in0(r0_q), .in1(r1_q), .in2(r2_q), .in3(r3_q), .in4(r4_q), .in5(r5_q), .in6(r6_q), .in7(r7_q),
    .in8(r8_q), .in9(r9_q), .in10(r10_q), .in11(r11_q), .in12(r12_q), .in13(r13_q), .in14(r14_q),
    .in15(r15_q), .in16(r16_q), .in17(r17_q), .in18(r18_q), .in19(r19_q), .in20(r20_q), .in21(r21_q),
    .in22(r22_q), .in23(r23_q), .in24(r24_q), .in25(r25_q), .in26(r26_q), .in27(r27_q), .in28(r28_q),
    .in29(r29_q), .in30(r30_q), .in31(r31_q), .out(Q2), .sel(N2));

  // Other names for the same wires on the sheet: RF_RESET = RESET

  // Notes on the sheet:
  //   输入引脚
  //   输出引脚
endmodule
