// Logisim project 时序发生器-7状态.circ as structural Verilog: 1 circuit, main circuit main
module main (
  input  En,
  input  skip,
  input  clk,
  input  clr,
  output M7,
  output M6,
  output M0,
  output M5,
  output M1,
  output M4,
  output M2,
  output M3
);

  wire [2:0] \_3位二进制数计数器_q ;

  Counter #(.width(3), .max('h7), .ongoal("wrap"), .trigger("rising"), .behavior("new")) \_3位二进制数计数器  (
    .load(skip), .D(3'b001), .count(En), .Q(\_3位二进制数计数器_q ), .clk(clk), .clr(clr));  // open: carry, preset, down
  // Probe on \_3位二进制数计数器_q 
  Decoder #(.select(3), .tristate("false"), .disabled("Z"), .enable("false")) decoder_1 (
    .out0(M0), .out1(M1), .out2(M2), .out3(M3), .out4(M4), .out5(M5), .out6(M6), .out7(M7),
    .sel(\_3位二进制数计数器_q ));
endmodule
