// Logisim project 黄浩链MIPS32CPU.circ as structural Verilog: 5 circuits, main circuit main
module main (
  input  in_1,
  input  reset,
  input  EN,
  input  reset_2
);

  wire ALU_X_sel, not_1_out, not_2_out, OF, R_MEM_HUANG021, RAM_Addr_s_HUANG021, S_Extend, SF, SKIP_HUANG021,
       W_F_HUANG021, W_GR_HUANG021, W_IR_HUANG021, W_MDR_HUANG021, W_MEM_HUANG021, W_PC_HUANG021, ZF,
       \指令译码逻辑_黄浩链021_1_add , \指令译码逻辑_黄浩链021_1_addi , \指令译码逻辑_黄浩链021_1_beq , \指令译码逻辑_黄浩链021_1_lw ,
       \指令译码逻辑_黄浩链021_1_or , \指令译码逻辑_黄浩链021_1_sub , \指令译码逻辑_黄浩链021_1_sw ;
  wire [1:0] ALU_Y_Sel, GR_D_S, PC_D_Sel_HUANG021, rd_rt_sel_HUANG021;
  wire [3:0] ALU_OP;
  wire [4:0] W_Addr;
  wire [5:0] funct, OP;
  wire [15:6] Imm;
  wire [23:11] cu_huang021_1_out_8;
  wire [27:18] PC_Target;
  wire [31:0] A, \A_黄浩链_q , B, F_HUANG, MDR, multiplexer_1_out, multiplexer_3_out, multiplexer_6_out,
       \n32位扩展器黄浩链_1_out_3 , PC, PC_4, PC_8, Q1, Q2, \RAM_黄浩链_data , shifter_1_out, undriven, W_Data;

  Multiplexer #(.select(2), .width(32), .disabled("Z"), .enable("false")) multiplexer_1 (
    .in0(PC_4), .in1(F_HUANG), .in2({PC_4[31:28], PC_Target, Imm, funct, 2'b00}), .in3(A),
    .out(multiplexer_1_out), .sel(PC_D_Sel_HUANG021));
  // Probe on PC
  // Probe on W_Addr
  Register #(.width(32), .trigger("falling"), .Select("high")) \PC_黄浩链  (
    .D(multiplexer_1_out), .en(W_PC_HUANG021), .Q(PC), .clk(in_1), .clr(reset_2));
  Multiplexer #(.select(2), .width(5), .disabled("Z"), .enable("false")) multiplexer_2 (
    .in0(PC_Target[22:18]), .in1(Imm[15:11]), .in2({5{1'b1}}), .out(W_Addr), .sel(rd_rt_sel_HUANG021));  // open: in3
  Multiplexer #(.select(1), .width(32), .disabled("Z"), .enable("false")) multiplexer_3 (
    .in0(PC), .in1(F_HUANG), .out(multiplexer_3_out), .sel(RAM_Addr_s_HUANG021));
  CU_HUANG021 cu_huang021_1 (
    .in_1(ZF), .in_2(OF),
    .out_8({cu_huang021_1_out_8, W_MDR_HUANG021, SKIP_HUANG021, W_GR_HUANG021, W_PC_HUANG021, W_F_HUANG021, S_Extend, ALU_X_sel, W_IR_HUANG021, R_MEM_HUANG021, W_MEM_HUANG021, RAM_Addr_s_HUANG021}),
    .rd_rt_sel(rd_rt_sel_HUANG021), .ALU_Y_sel(ALU_Y_Sel), .GR_D_sel(GR_D_S), .PC_D_SEL(PC_D_Sel_HUANG021),
    .ALU_OP(ALU_OP), .in_3(EN), .in_4(in_1), .in_5(OP), .in_7(funct), .in_6(reset_2));
  // Probe on B
  // Probe on Q1
  // Probe on multiplexer_3_out[7:0]
  not not_1 (not_1_out, in_1);
  RF_32_main main_1 (
    .N1(PC_Target[27:23]), .N2(PC_Target[22:18]), .ND(W_Addr), .D_in(W_Data), .WRITEREG(W_GR_HUANG021),
    .CLK(not_1_out), .RESET(reset_2), .Q1(Q1), .Q2(Q2));
  Multiplexer #(.select(2), .width(32), .disabled("Z"), .enable("false")) multiplexer_4 (
    .in0(F_HUANG), .in1(32'h1), .in2({32{1'b0}}), .in3(MDR), .out(W_Data), .sel(GR_D_S));
  // Probe on W_Data
  \时序发生器_7状态_main  main_2 (
    .En(EN), .skip(SKIP_HUANG021), .clk(in_1), .clr(reset));  // open: M0, M1, M2, M7, M6, M5, M4, M3
  not not_2 (not_2_out, in_1);
  Register #(.width(32), .trigger("falling"), .Select("high")) \A_黄浩链  (
    .D(Q1), .en(1'b1), .Q(\A_黄浩链_q ), .clk(in_1));  // open: clr
  Register #(.width(32), .trigger("falling"), .Select("low")) \B_黄浩链  (
    .D(Q2), .en(1'b1), .Q(B), .clk(in_1), .clr(reset_2));
  RAM #(.addrWidth(8), .dataWidth(32), .bus("separate"), .Select("high")) \RAM_黄浩链  (
    .addr(multiplexer_3_out[7:0]), .din(B), .data(\RAM_黄浩链_data ), .str(W_MEM_HUANG021), .clk(not_2_out),
    .ld(R_MEM_HUANG021));  // open: sel, clr
  \_32位扩展器黄浩链  \u_32位扩展器黄浩链_1  (.D_lin({Imm, funct}), .D_sel_Huang(S_Extend), .out_3(\n32位扩展器黄浩链_1_out_3 ));
  // Probe on F_HUANG
  // Probe on \RAM_黄浩链_data 
  Multiplexer #(.select(1), .width(32), .disabled("Z"), .enable("false")) multiplexer_5 (
    .in0(PC), .in1(\A_黄浩链_q ), .out(A), .sel(ALU_X_sel));
  Shifter #(.width(32), .shift("ll")) shifter_1 (.in(\n32位扩展器黄浩链_1_out_3 ), .\dist (5'b00010), .out(shifter_1_out));
  // Probe on Q2
  Multiplexer #(.select(2), .width(32), .disabled("Z"), .enable("false")) multiplexer_6 (
    .in0(32'h4), .in1(B), .in2(\n32位扩展器黄浩链_1_out_3 ), .in3(shifter_1_out), .out(multiplexer_6_out),
    .sel(ALU_Y_Sel));
  \指令译码逻辑_黄浩链021  \u_指令译码逻辑_黄浩链021_1  (
    .OP(OP), .Funct(funct), .ADD(\指令译码逻辑_黄浩链021_1_add ), .SW(\指令译码逻辑_黄浩链021_1_sw ),
    .BEQ(\指令译码逻辑_黄浩链021_1_beq ), .ADDI(\指令译码逻辑_黄浩链021_1_addi ), .LW(\指令译码逻辑_黄浩链021_1_lw ),
    .OR(\指令译码逻辑_黄浩链021_1_or ), .SUB(\指令译码逻辑_黄浩链021_1_sub ));
  Register #(.width(32), .trigger("falling"), .Select("low")) \MDR_黄浩链  (
    .D(\RAM_黄浩链_data ), .en(W_MDR_HUANG021), .Q(MDR), .clk(in_1), .clr(reset_2));
  Register #(.width(32), .trigger("falling"), .Select("low")) \IR_黄浩链  (
    .D(\RAM_黄浩链_data ), .en(W_IR_HUANG021), .Q({OP, PC_Target, Imm, funct}), .clk(in_1), .clr(reset_2));
  \黄浩链20212132021ALU  \u_黄浩链20212132021alu_1  (
    .in_1(A), .in_2(multiplexer_6_out), .\移位位数sa (Imm[10:6]), .F(PC_4), .ALU_OP_021(ALU_OP), .OF(OF),
    .SF(SF), .ZF(ZF));
  Adder #(.width(32)) adder_1 (.a(PC_4), .b(undriven), .out(PC_8));  // open: cin, cout
  Register #(.width(32), .trigger("falling"), .Select("low")) \F_黄浩链  (
    .D(PC_4), .en(W_F_HUANG021), .Q(F_HUANG), .clk(in_1), .clr(reset_2));

  // Other names for the same wires on the sheet: clk = in_1; PC_Target (some bits) = {PC_4[31:28], Imm, funct};
  //   Imm[5:0] = funct; Target[25:0] = {PC_Target, Imm, funct}; Sa[4:0] = Imm[10:6]; rd[4:0] = Imm[15:11];
  //   rt[4:0] = PC_Target[22:18]; rs[4:0] = PC_Target[27:23]; CLEAR = reset_2; reset_t = reset_2

  // Notes on the sheet:
  //   PC
  //   W_Addr
  //   Q1
  //   W_Data
  //   F
  //   Q2
endmodule

module \黄浩链20212132021ALU  (
  input  [31:0] in_1,
  input  [31:0] in_2,
  input  [3:0] ALU_OP_021,
  input  [4:0] \移位位数sa ,
  output [31:0] F,
  output OF,
  output SF,
  output ZF
);

  wire adder_2_cout, adder_3_cout, adder_4_cout, adder_5_cout, \S有符号减溢出 , \S有符号加溢出 ;
  wire [31:0] not_1_out, \S与运算 , \S异或运算 , \S或运算 , \S无符号减 , \S无符号加 , \S有符号减 , \S有符号加 , \S算术右移 , \S逻辑右移 ,
       \S逻辑左移 ;

  // Probe on in_1
  // Probe on in_2
  assign not_1_out = ~in_2;  // NOT_Gate not_1, 32 bits wide
  Adder #(.width(32)) adder_1 (.a(in_1), .b(in_2), .out(\S无符号加 ), .cin(1'b0));  // open: cout
  Subtractor #(.width(32)) subtractor_1 (.a(in_1), .b(in_2), .out(\S无符号减 ), .bin(1'b0));  // open: bout
  Adder #(.width(31)) adder_2 (.a(in_1[30:0]), .b(in_2[30:0]), .out(\S有符号加 [30:0]), .cin(1'b0), .cout(adder_2_cout));
  Adder #(.width(1)) adder_3 (.a(in_1[31]), .b(in_2[31]), .out(\S有符号加 [31]), .cin(adder_2_cout), .cout(adder_3_cout));
  Comparator #(.width(32), .mode("twosComplement")) comparator_1 (.a(in_1), .b(in_2), .lt(SF));  // open: gt, eq
  assign \S与运算  = in_1 & in_2;  // AND_Gate and_1, 32 bits wide
  assign \S或运算  = in_1 | in_2;  // OR_Gate or_1, 32 bits wide
  assign \S异或运算  = in_1 ^ in_2;  // XOR_Gate xor_1, 32 bits wide
  Shifter #(.width(32), .shift("ll")) shifter_1 (.in(in_2), .\dist (\移位位数sa ), .out(\S逻辑左移 ));
  Shifter #(.width(32), .shift("lr")) shifter_2 (.in(in_2), .\dist (\移位位数sa ), .out(\S逻辑右移 ));
  Shifter #(.width(32), .shift("ar")) shifter_3 (.in(in_2), .\dist (\移位位数sa ), .out(\S算术右移 ));
  Adder #(.width(31)) adder_4 (
    .a(in_1[30:0]), .b(not_1_out[30:0]), .out(\S有符号减 [30:0]), .cin(1'b1), .cout(adder_4_cout));
  Adder #(.width(1)) adder_5 (
    .a(in_1[31]), .b(not_1_out[31]), .out(\S有符号减 [31]), .cin(adder_4_cout), .cout(adder_5_cout));
  xor xor_2 (\S有符号加溢出 , adder_2_cout, adder_3_cout);
  xor xor_3 (\S有符号减溢出 , adder_4_cout, adder_5_cout);
  nor nor_1 (ZF, F[31], F[30], F[29], F[28], F[27], F[26], F[25], F[24], F[23], F[22], F[21], F[20], F[19], F[18], F[17], F[16], F[15], F[14], F[13], F[12], F[11], F[10], F[9], F[8], F[7], F[6], F[5], F[4], F[3], F[2], F[1], F[0]);
  Multiplexer #(.select(4), .width(32), .disabled("Z"), .enable("false")) multiplexer_1 (
    .in0({32{1'b0}}), .in1(\S有符号加 ), .in2(\S无符号加 ), .in3(\S有符号减 ), .in4(\S无符号减 ), .in5(\S与运算 ), .in6(\S或运算 ),
    .in7(\S异或运算 ), .in8({32{1'b0}}), .in9(\S逻辑左移 ), .in10(\S逻辑右移 ), .in11(\S算术右移 ), .in12({32{1'b0}}),
    .in13({32{1'b0}}), .in14({32{1'b0}}), .in15({32{1'b0}}), .out(F), .sel(ALU_OP_021));
  Multiplexer #(.select(4), .width(1), .disabled("Z"), .enable("false")) multiplexer_2 (
    .in0(1'b0), .in1(\S有符号加溢出 ), .in2(1'b0), .in3(\S有符号减溢出 ), .in4(1'b0), .in5(1'b0), .in6(1'b0), .in7(1'b0),
    .in8(1'b0), .in9(1'b0), .in10(1'b0), .in11(1'b0), .in12(1'b0), .in13(1'b0), .in14(1'b0), .in15(1'b0),
    .out(OF), .sel(ALU_OP_021));

  // Notes on the sheet:
  //   X_IN
  //   Y_IN
  //   Y补码
  //   Y_IN
  //   X补码
  //   比较器
  //   与运算
  //   或运算
  //   异或运算
  //   逻辑左移
  //   逻辑右移
  //   算术右移
  //   无符号加法
  //   无符号减法
  //   有符号数加法溢出位检测
  //   有符号数减法溢出位检测
endmodule

module \_32位扩展器黄浩链  (
  input  [15:0] D_lin,
  input  D_sel_Huang,
  output [31:0] out_3
);

  wire [31:0] bit_extender_1_out, bit_extender_2_out;

  assign bit_extender_1_out = {{16{1'b0}}, D_lin};  // Bit_Extender bit_extender_1
  assign bit_extender_2_out = {{16{1'b0}}, D_lin};  // Bit_Extender bit_extender_2
  Multiplexer #(.select(1), .width(32), .disabled("Z"), .enable("false")) multiplexer_1 (
    .in0(bit_extender_1_out), .in1(bit_extender_2_out), .out(out_3), .sel(D_sel_Huang));

  // Notes on the sheet:
  //   0扩展
  //   符号扩展
endmodule

module \指令译码逻辑_黄浩链021  (
  input  [5:0] OP,
  input  [5:0] Funct,
  output BEQ,
  output ADD,
  output SW,
  output ADDI,
  output LW,
  output OR,
  output SUB
);

  wire and_3_out, and_6_out, nor_1_out, not_1_out, not_2_out, not_3_out, not_4_out, not_5_out, not_6_out,
       not_7_out, not_8_out, not_9_out, not_10_out, not_12_out, not_13_out, not_14_out, R;

  not not_1 (not_1_out, OP[4]);
  not not_2 (not_2_out, OP[2]);
  not not_3 (not_3_out, Funct[4]);
  not not_4 (not_4_out, Funct[3]);
  not not_5 (not_5_out, Funct[2]);
  not not_6 (not_6_out, Funct[0]);
  and and_1 (SW, OP[5], not_1_out, OP[3], not_2_out, OP[1], OP[0]);
  nor nor_1 (nor_1_out, Funct[0], Funct[1], Funct[2], Funct[3], Funct[4]);
  not not_7 (not_7_out, OP[4]);
  not not_8 (not_8_out, OP[3]);
  not not_9 (not_9_out, OP[2]);
  not not_10 (not_10_out, Funct[4]);
  and and_2 (ADD, nor_1_out, Funct[5], R);
  not not_11 (not_10_out, Funct[3]);
  not not_12 (not_12_out, Funct[1]);
  and and_3 (and_3_out, Funct[5], not_3_out, not_4_out, not_5_out, Funct[1], not_6_out);
  and and_4 (LW, OP[5], not_7_out, not_8_out, not_9_out, OP[1], OP[0]);
  and and_5 (SUB, R, and_3_out);
  and and_6 (and_6_out, Funct[5], not_10_out, not_10_out, Funct[2], not_12_out, Funct[0]);
  and and_7 (OR, R, and_6_out);
  nor nor_2 (R, OP[0], OP[1], OP[2], OP[3], OP[4], OP[5]);
  not not_13 (not_13_out, OP[2]);
  not not_14 (not_14_out, OP[3]);
  nor nor_3 (BEQ, OP[5], OP[4], OP[3], not_13_out, OP[1], OP[0]);
  nor nor_4 (ADDI, OP[5], OP[4], not_14_out, OP[2], OP[1], OP[0]);

  // Other names for the same wires on the sheet: I0 = Funct[0]; I1 = Funct[1]; I2 = Funct[2]; I3 = Funct[3];
  //   I4 = Funct[4]; I5 = Funct[5]; I26 = OP[0]; I27 = OP[1]; I28 = OP[2]; I29 = OP[3]; I30 = OP[4]; I31 = OP[5]
endmodule

module CU_HUANG021 (
  input  in_1,
  input  in_2,
  input  in_3,
  input  in_4,
  input  [5:0] in_5,
  input  in_6,
  input  [5:0] in_7,
  output [23:0] out_8,
  output [1:0] rd_rt_sel,
  output [1:0] ALU_Y_sel,
  output [1:0] GR_D_sel,
  output [1:0] PC_D_SEL,
  output [3:0] ALU_OP
);

  wire ADD_HUANG021, ADDI_HUANG021, and_1_out, and_2_out, and_3_out, and_4_out, and_5_out, and_7_out,
       and_8_out, and_9_out, and_12_out, and_14_out, and_15_out, and_16_out, and_17_out, and_18_out,
       and_19_out, and_20_out, and_21_out, and_22_out, and_23_out, and_24_out, and_25_out, and_26_out,
       and_30_out, and_31_out, BEQ_HUANG021, LW_HUANG021, M2_HUANG021, M3_HUANG021, M4_HUANG021, M5_HUANG021,
       not_1_out, not_2_out, not_3_out, not_4_out, or_1_out, or_2_out, or_3_out, or_4_out, or_5_out,
       or_10_out, or_12_out, or_14_out, or_17_out, or_20_out, OR_HUANG021, SUB_HUANG021, SW_HUANG021;

  not not_1 (not_1_out, in_2);
  not not_2 (not_2_out, in_2);
  not not_3 (not_3_out, in_2);
  not not_4 (not_4_out, in_2);
  and and_1 (and_1_out, LW_HUANG021, M5_HUANG021);
  or or_1 (or_1_out, LW_HUANG021, ADD_HUANG021, OR_HUANG021, ADDI_HUANG021, SW_HUANG021, SUB_HUANG021);
  or or_2 (or_2_out, OR_HUANG021, SUB_HUANG021, ADD_HUANG021);
  and and_2 (and_2_out, not_1_out, ADD_HUANG021);
  and and_3 (and_3_out, not_2_out, OR_HUANG021);
  and and_4 (and_4_out, not_3_out, ADDI_HUANG021);
  and and_5 (and_5_out, not_4_out, SUB_HUANG021);
  and and_6 (rd_rt_sel[0], or_2_out, M4_HUANG021);
  and and_7 (and_7_out, BEQ_HUANG021, M2_HUANG021);
  and and_8 (and_8_out, M3_HUANG021, or_1_out);
  or or_3 (or_3_out, and_2_out, and_3_out, and_4_out, and_5_out);
  and and_9 (and_9_out, M4_HUANG021, LW_HUANG021);
  or or_4 (or_4_out, BEQ_HUANG021, LW_HUANG021, ADD_HUANG021, SUB_HUANG021, SW_HUANG021, ADDI_HUANG021, OR_HUANG021);
  and and_10 (PC_D_SEL[0], M3_HUANG021, BEQ_HUANG021);
  or or_5 (or_5_out, SW_HUANG021, LW_HUANG021, ADDI_HUANG021);
  and and_11 (out_8[1], M4_HUANG021, SW_HUANG021);
  or or_6 (out_8[0], and_9_out, and_12_out);
  and and_12 (and_12_out, SW_HUANG021, M4_HUANG021);
  and and_13 (out_8[4], or_4_out, M3_HUANG021);
  or or_7 (out_8[6], and_7_out, and_8_out);
  and and_14 (and_14_out, or_3_out, M4_HUANG021);
  \指令译码逻辑_黄浩链021  \u_指令译码逻辑_黄浩链021_1  (
    .OP(in_5), .Funct(in_7), .ADD(ADD_HUANG021), .SW(SW_HUANG021), .BEQ(BEQ_HUANG021), .ADDI(ADDI_HUANG021),
    .LW(LW_HUANG021), .OR(OR_HUANG021), .SUB(SUB_HUANG021));
  or or_8 (out_8[8], and_14_out, and_1_out);
  and and_15 (and_15_out, or_5_out, M3_HUANG021);
  and and_16 (and_16_out, M2_HUANG021, BEQ_HUANG021);
  \时序发生器_7状态_main  main_1 (
    .En(in_3), .skip(out_8[9]), .clk(in_4), .M1(out_8[3]), .clr(in_6), .M2(M2_HUANG021), .M5(M5_HUANG021),
    .M4(M4_HUANG021), .M3(M3_HUANG021));  // open: M0, M7, M6
  or or_9 (ALU_Y_sel[1], and_15_out, and_16_out);
  and and_17 (and_17_out, LW_HUANG021, M4_HUANG021);
  and and_18 (and_18_out, BEQ_HUANG021, M2_HUANG021);
  or or_10 (or_10_out, ADD_HUANG021, OR_HUANG021, SUB_HUANG021, BEQ_HUANG021);
  and and_19 (and_19_out, BEQ_HUANG021, M2_HUANG021);
  or or_11 (out_8[2], out_8[3], and_17_out);
  or or_12 (or_12_out, BEQ_HUANG021, ADD_HUANG021, ADDI_HUANG021, LW_HUANG021, SW_HUANG021, SUB_HUANG021);
  or or_13 (ALU_OP[0], and_22_out, and_18_out);
  and and_20 (and_20_out, M3_HUANG021, or_14_out);
  or or_14 (or_14_out, BEQ_HUANG021, SUB_HUANG021, OR_HUANG021);
  and and_21 (and_21_out, or_10_out, M3_HUANG021);
  and and_22 (and_22_out, M3_HUANG021, or_12_out);
  or or_15 (ALU_Y_sel[0], and_21_out, and_19_out);
  or or_16 (ALU_OP[1], and_20_out, out_8[3]);
  or or_17 (or_17_out, ADD_HUANG021, OR_HUANG021, SUB_HUANG021, ADDI_HUANG021, SW_HUANG021);
  and and_23 (and_23_out, BEQ_HUANG021, in_1);
  and and_24 (and_24_out, M3_HUANG021, BEQ_HUANG021);
  and and_25 (and_25_out, or_17_out, M4_HUANG021);
  and and_26 (and_26_out, LW_HUANG021, M5_HUANG021);
  or or_18 (out_8[9], and_24_out, and_25_out, and_26_out);
  or or_19 (out_8[7], out_8[3], and_23_out);
  and and_27 (out_8[10], LW_HUANG021, M4_HUANG021);
  and and_28 (GR_D_sel[1], M5_HUANG021, LW_HUANG021);
  or or_20 (or_20_out, ADDI_HUANG021, LW_HUANG021, SW_HUANG021);
  and and_29 (ALU_OP[2], OR_HUANG021, M3_HUANG021);
  and and_30 (and_30_out, or_20_out, M3_HUANG021);
  and and_31 (and_31_out, BEQ_HUANG021, M2_HUANG021);
  or or_21 (out_8[5], and_30_out, and_31_out);

  assign ALU_OP[3] = 1'b0;
  assign GR_D_sel[0] = GR_D_sel[1];
  assign PC_D_SEL[1] = 1'b0;
  assign rd_rt_sel[1] = 1'b0;

  // Other names for the same wires on the sheet: ALU_OP_0 = ALU_OP[0]; ALU_OP_1 = ALU_OP[1]; ALU_OP_2 = ALU_OP[2];
  //   ALU_Y_sel_0 = ALU_Y_sel[0]; ALU_Y_sel_1 = ALU_Y_sel[1]; CLK = in_4; EN = in_3; FUNCT[5:0] = in_7;
  //   GR_D_s_HUANG021_0 = GR_D_sel[1]; GR_D_s_HUANG_021_1 = GR_D_sel[1]; OF = in_2; OP[5:0] = in_5;
  //   RAM_Addr_s_HUANG021 = out_8[0]; W_RAM_HUANG021 = out_8[1]; R_MEN_HUANG021 = out_8[2]; M1_HUANG021 = out_8[3];
  //   W_IR_HUANG021 = out_8[3]; ALU_X_sel = out_8[4]; S_Extend = out_8[5]; W_F_HUANG021 = out_8[6];
  //   W_PC_HUANG021 = out_8[7]; W_GR_HUANG021 = out_8[8]; SKIP_HUANG021 = out_8[9]; W_MDR_HUANG021 = out_8[10];
  //   PC_D_SEL_HUANG021_0 = PC_D_SEL[0]; rd_rt_sel_HUANG021_0 = rd_rt_sel[0]; ZF = in_1
endmodule
